# Fritzing sketch PDM_Predictive_Maintenance (saved by Fritzing 0.9.3)
breadboards: 1

parts:
  U1_Raspberry_Pi_4 = Raspberry Pi 4B
  U2_ADXL345 = Triple Axis Accelerometer Breakout - ADXL345
  U3_MAX6675 = MAX6675 K-type thermocouple module
  U4_INMP441 = INMP441 I2S MEMS microphone
  R1_K-type_probe = K-type thermocouple probe (class 1)
  R2 = Resistor [resistance=10k tolerance=1% power=0.25W package=THT]
  R4 = Resistor [resistance=330 tolerance=5% power=0.25W package=THT]
  C1 = Ceramic Capacitor [capacitance=100nF voltage=16V package="100 mil [THT, multilayer]"]
  C2 = Ceramic Capacitor [capacitance=100nF voltage=16V package="100 mil [THT, multilayer]"]
  C3 = Ceramic Capacitor [capacitance=100nF voltage=16V package="100 mil [THT, multilayer]"]
  C4 = Electrolytic Capacitor [capacitance=10uF voltage=16V package="100 mil [THT, electrolytic]"]
  D1 = Red LED - 5mm [package="5 mm [THT]"]
  F1_5V_fan = 5 V cooling fan 30 mm

nets:
  3V3: U1_Raspberry_Pi_4.3V3, U2_ADXL345.VCC, U2_ADXL345.CS, U3_MAX6675.VIN, U4_INMP441.VDD, R2.Pin_1, C1.0, C2.0, C3.0, C4.+
  5V: U1_Raspberry_Pi_4.5V, F1_5V_fan.+5V
  N1: U1_Raspberry_Pi_4.GPIO2, U2_ADXL345.SDA
  N2: U1_Raspberry_Pi_4.GPIO3, U2_ADXL345.SCL
  GND: U1_Raspberry_Pi_4.GND, U2_ADXL345.GND, U2_ADXL345.SDO, U3_MAX6675.GND, U4_INMP441.GND, U4_INMP441.LR, C1.1, C2.1, C3.1, C4.-, D1.cathode, F1_5V_fan.GND
  N3: U1_Raspberry_Pi_4.GPIO18, U4_INMP441.BCLK
  N4: U1_Raspberry_Pi_4.GPIO9, U3_MAX6675.SO
  N5: U1_Raspberry_Pi_4.GPIO11, U3_MAX6675.SCLK
  N6: U1_Raspberry_Pi_4.GPIO8, U3_MAX6675.CS, R2.Pin_0
  N7: U1_Raspberry_Pi_4.GPIO19, U4_INMP441.WS
  N8: U1_Raspberry_Pi_4.GPIO16, R4.Pin_1
  N9: U1_Raspberry_Pi_4.GPIO20, U4_INMP441.SD
  N10: U3_MAX6675.T+, R1_K-type_probe.T+
  N11: U3_MAX6675.T-, R1_K-type_probe.T-
  N12: R4.Pin_0, D1.anode

custom parts:
  Raspberry Pi 4B: The RPi4B, a faster version of the awesome Raspberry Pi 3 ARM Board with 40 pin gpio. Ready for special Raspberry Pi B+ and RPi2 Hat (Hardware attached (on) top) new features: The most surprising change for the Pi 4B is that it is available with three different amounts of fast DDR4 SDRAM memory; 1GB, 2GB, or 4GB. Combined with a newer 1.5GHz quad-core processor, the Pi 4B can run larger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
  Triple Axis Accelerometer Breakout - ADXL345: Description: This new version adds 2 standoff holes as well as an extra decoupling capacitor. The ADXL345 is a small, thin, low power, 3-axis accelerometer with high resolution (13-bit) measurement at up to ±16 g. Digital output data is formatted as 16-bit twos complement and is accessible through either a SPI (3- or 4-wire) or I2C digital interface. The ADXL345 is well suited to measures the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
  220 Ω Resistor: A generic resistor (0.25W)
  Ceramic Capacitor: 100 nF multilayer Ceramic Capacitor
  Electrolytic Capacitor: A small electrolytic capacitor
  Red LED - 5mm: A generic red LED (~1.8V)
